# Fritzing sketch SmartSensor (saved by Fritzing 0.9.3b)
breadboards: 1

parts:
  PIR1 = PIR sensor
  S1 = Pushbutton [package="[THT]"]
  S2 = Pushbutton [package="[THT]"]
  S3 = Pushbutton [package="[THT]"]
  R1 = Rotary Potentiometer (Small) [maximum_resistance=100kΩ package=THT]
  R2 = Resistor [tolerance=±5% resistance=10k package=THT]
  R3 = Resistor [tolerance=±5% resistance=10k package=THT]
  R4 = Resistor [tolerance=±5% resistance=10k package=THT]
  R5 = Resistor [tolerance=±5% resistance=220 package=THT]
  R6 = Resistor [tolerance=±5% resistance=220 package=THT]
  LED1 = LED - 5mm [color="Red (633nm)" package="5 mm [THT]"]
  LED2 = LED - 5mm [color="Red (633nm)" package="5 mm [THT]"]
  Componente1 = Arduino Uno (Rev3)
  HC-SR04_Sensor_1 = HC-SR04 Ultrasonic Distance Sensor
  J1 = Basic Servo

nets:
  VCC: PIR1.VDD, S1.Pin_3, S1.Pin_4, S2.Pin_3, S2.Pin_4, S3.Pin_3, S3.Pin_4, R1.leg2, Componente1.5V, HC-SR04_Sensor_1.VCC, J1.vcc
  N1: PIR1.SIG, Componente1.D2
  GND: PIR1.GND, R1.leg1, R2.Pin_1, R3.Pin_1, R4.Pin_1, LED1.cathode, LED2.cathode, Componente1.GND, HC-SR04_Sensor_1.GND, J1.gnd
  N2: S1.Pin_1, S1.Pin_2, R2.Pin_0, Componente1.D5_PWM
  N3: S2.Pin_1, S2.Pin_2, R3.Pin_0, Componente1.D4
  N4: S3.Pin_1, S3.Pin_2, R4.Pin_0, Componente1.D3_PWM
  N5: R1.wiper, Componente1.A0
  N6: R5.Pin_0, LED1.anode
  N7: R5.Pin_1, Componente1.D7
  N8: R6.Pin_0, Componente1.D6_PWM
  N9: R6.Pin_1, LED2.anode
  N10: Componente1.D9_PWM, J1.pulse
  N11: Componente1.D10_PWM/SS, HC-SR04_Sensor_1.ECHO
  N12: Componente1.D11_PWM/MOSI, HC-SR04_Sensor_1.TRIG
